// Logisim project CPU.circ as structural Verilog: 7 circuits, main circuit main
module main (
  input  [17:0] in_1,
  input  in_2,
  input  in_3,
  input  in_4,
  input  [3:0] in_5,
  output [17:0] out_6
);

  wire and_1_out, and_2_out, and_3_out, B0, B1, B2, B3, B4, B5, B6, B7, B8, B9, B10, B11, clock_1_out, D15,
       I0, I1, I2, I3, not_1_out, T3;
  wire [14:0] instruction_decoder_1_opt_code;

  RAM #(.addrWidth(16), .dataWidth(18)) ram_1 ();  // open: addr, data, sel, clk, ld, clr
  Clock clock_1 (.out(clock_1_out));
  Timer timer_1 (
    .Clock(clock_1_out), .T3(T3));  // open: Increment, Clear, T0, T1, T2, T4, T5, T6, T7, T8, T9, T10, T11, T12, T13, T14, T15, Overflow
  // Bus bus_1: pin names not known; wires that end beside it: in_1, in_3, in_4, clock_1_out
  Instruction_Decoder instruction_decoder_1 (
    ._18_Bit_Input(in_1), .Enable(in_2), .Addressing_Mode({I3, I2, I1, I0}),
    .Opt_Code({D15, instruction_decoder_1_opt_code}),
    .Data({B11, B10, B9, B8, B7, B6, B5, B4, B3, B2, B1, B0}));
  and and_1 (and_1_out, I0, D15, T3);
  not not_1 (not_1_out, and_2_out);
  and and_2 (and_2_out, B0, B1, B2, B3, B4, B5, B6, B7, B8, B9, B10, B11);
  and and_3 (and_3_out, and_1_out, not_1_out);
  Register #(.width(12)) Accumulator (.clr(and_3_out));  // open: D, en, Q, clk
endmodule

module Timer (
  input  Increment,
  input  Clock,
  input  Clear,
  output T0,
  output T1,
  output T2,
  output T3,
  output T4,
  output T5,
  output T6,
  output T7,
  output T8,
  output T9,
  output T10,
  output T11,
  output T12,
  output T13,
  output T14,
  output T15,
  output Overflow
);

  wire [3:0] counter_1_q;

  Counter #(.width(4), .max('hf)) counter_1 (
    .count(Increment), .Q(counter_1_q), .carry(Overflow), .clk(Clock), .clr(Clear));  // open: load, D
  Decoder #(.select(4)) decoder_1 (
    .out0(T0), .out1(T1), .out2(T2), .out3(T3), .out4(T4), .out5(T5), .out6(T6), .out7(T7), .out8(T8),
    .out9(T9), .out10(T10), .out11(T11), .out12(T12), .out13(T13), .out14(T14), .out15(T15), .sel(counter_1_q));  // open: en
endmodule

// ID
module Instruction_Decoder (
  input  [17:0] _18_Bit_Input,
  input  Enable,
  output [3:0] Addressing_Mode,
  output [15:0] Opt_Code,
  output [11:0] Data
);

  Decoder #(.select(2)) decoder_1 (
    .out0(Addressing_Mode[0]), .out1(Addressing_Mode[1]), .out2(Addressing_Mode[2]),
    .out3(Addressing_Mode[3]), .sel(_18_Bit_Input[17:16]), .en(Enable));
  Decoder #(.select(4)) decoder_2 (
    .out0(Opt_Code[0]), .out1(Opt_Code[1]), .out2(Opt_Code[2]), .out3(Opt_Code[3]), .out4(Opt_Code[4]),
    .out5(Opt_Code[5]), .out6(Opt_Code[6]), .out7(Opt_Code[7]), .out8(Opt_Code[8]), .out9(Opt_Code[9]),
    .out10(Opt_Code[10]), .out11(Opt_Code[11]), .out12(Opt_Code[12]), .out13(Opt_Code[13]),
    .out14(Opt_Code[14]), .out15(Opt_Code[15]), .sel(_18_Bit_Input[15:12]), .en(Enable));

  assign Data = _18_Bit_Input[11:0];

  // Other names for the same wires on the sheet: ENB = Enable
endmodule

module Bus (
  input  [2:0] in_1
);

  wire AC, and_1_out, AR, DR, IR, IX, MR, not_1_out, or_1_out, or_2_out, PC, R, T0, TR;
  wire [11:0] AC_q, AR_q, DR_q, IX_q, n18b212b_1__12b_output, n18b212b_2__12b_output, n18b212b_3__12b_output,
       n18b212b_4__12b_output, n18b212b_5__12b_output, n18b212b_6__12b_output, PC_q, TR_q;
  wire [17:0] IR_q, multiplexer_1_out, n12b218b_1__18b_output, n12b218b_2__18b_output,
       n12b218b_3__18b_output, n12b218b_4__18b_output, n12b218b_5__18b_output;

  _18B212B u_18b212b_1 (._12b_Output(n18b212b_1__12b_output), ._18b_input(multiplexer_1_out));
  Multiplexer #(.select(3), .width(18)) multiplexer_1 (
    .in0(n12b218b_1__18b_output), .in1(n12b218b_2__18b_output), .in2(n12b218b_3__18b_output),
    .in3(n12b218b_4__18b_output), .in4(n12b218b_5__18b_output), .in5(IR_q), .out(multiplexer_1_out),
    .sel(in_1));  // open: in6, in7, en
  _12B218B u_12b218b_1 (._12b_Input(IX_q), ._18b_output(n12b218b_1__18b_output));
  Register #(.width(12)) u_IX (.D(n18b212b_1__12b_output), .Q(IX_q));  // open: en, clk, clr
  Decoder #(.select(3)) decoder_1 (
    .out0(IX), .out1(AR), .out2(PC), .out3(AC), .out4(IR), .out5(TR), .out6(MR), .sel(in_1));  // open: out7, en
  _18B212B u_18b212b_2 (._12b_Output(n18b212b_2__12b_output), ._18b_input(multiplexer_1_out));
  or or_1 (or_1_out, PC, IR, AC);
  _12B218B u_12b218b_2 (._12b_Input(AR_q), ._18b_output(n12b218b_2__18b_output));
  Register #(.width(12)) u_AR (.D(n18b212b_2__12b_output), .en(or_1_out), .Q(AR_q));  // open: clk, clr
  _18B212B u_18b212b_3 (._12b_Output(n18b212b_3__12b_output), ._18b_input(multiplexer_1_out));
  Register #(.width(1)) u_R (.Q(R));  // open: D, en, clk, clr
  Register #(.width(12)) u_PC (.D(n18b212b_3__12b_output), .en(AR), .Q(PC_q));  // open: clk, clr
  _12B218B u_12b218b_3 (._12b_Input(PC_q), ._18b_output(n12b218b_3__18b_output));
  _18B212B u_18b212b_4 (._12b_Output(n18b212b_4__12b_output), ._18b_input(multiplexer_1_out));
  Register #(.width(12)) u_DR (.D(n18b212b_4__12b_output), .en(IX), .Q(DR_q));  // open: clk, clr
  _12B218B u_12b218b_4 (._12b_Input(DR_q), ._18b_output(n12b218b_4__18b_output));
  _18B212B u_18b212b_5 (._12b_Output(n18b212b_5__12b_output), ._18b_input(multiplexer_1_out));
  Register #(.width(12)) u_AC (.D(n18b212b_5__12b_output), .en(DR), .Q(AC_q));  // open: clk, clr
  _12B218B u_12b218b_5 (._12b_Input(AC_q), ._18b_output(n12b218b_5__18b_output));
  Register #(.width(18)) u_IR (.D(multiplexer_1_out), .Q(IR_q));  // open: en, clk, clr
  _18B212B u_18b212b_6 (._12b_Output(n18b212b_6__12b_output), ._18b_input(multiplexer_1_out));
  or or_2 (or_2_out, DR, and_1_out);
  and and_1 (and_1_out, not_1_out, T0);
  not not_1 (not_1_out, R);
  _12B218B u_12b218b_6 (._12b_Input(TR_q), ._18b_output(IR_q));
  Register #(.width(12)) u_TR (.D(n18b212b_6__12b_output), .en(or_2_out), .Q(TR_q));  // open: clk, clr
endmodule

module _18B212B (
  input  [17:0] _18b_input,
  output [11:0] _12b_Output
);


  assign _12b_Output = _18b_input[11:0];

  // Notes on the sheet:
  //   TODO: Manage orientation of these lines
endmodule

module _12B218B (
  input  [11:0] _12b_Input,
  output [17:0] _18b_output
);


  assign _18b_output = {{6{1'b0}}, _12b_Input};

  // Notes on the sheet:
  //   TODO: Manage orientation of these lines
endmodule

module Memory (
  input  [17:0] in_1,
  input  in_2,
  input  [11:0] in_3
);

  wire clock_1_out;

  RAM #(.addrWidth(12), .dataWidth(18)) ram_1 (
    .addr(in_3), .data(in_1), .clk(clock_1_out), .ld(in_2));  // open: sel, clr
  Clock clock_1 (.out(clock_1_out));
endmodule
